// Digital circuit frontpanel.dig as structural Verilog
module frontpanel (
  input  [15:0] A,
  input  [7:0] SD,
  output [15:0] R0,
  output [15:0] R1,
  output [15:0] R2,
  output [15:0] R3,
  output [15:0] B,
  output [1:0] rs,
  output [1:0] rd,
  output [15:0] A_2
);

  wire button_1_out, button_2_out;
  wire [1:0] PC_out;
  wire [15:0] execute_1_p3;
  wire [31:0] Program_d;

  Button button_1 (.out(button_1_out));
  Counter #(.Bits(2)) PC (.en(1'b1), .C(button_2_out), .clr(1'b0), .out(PC_out));  // open: ovf
  Button button_2 (.out(button_2_out));
  EEPROMDualPort #(.Bits(32), .isProgramMemory("true")) Program (
    .A(PC_out), .Din({{8{1'b0}}, SD, A}), .str(1'b1), .C(button_1_out), .ld(1'b1), .D(Program_d));
  // decoder decoder_1: pin names not known; wires that end beside it: Program_d, A_2, rs, rd
  // execute execute_1: pin names not known; wires that end beside it: A_2, B, execute_1_p3
  regfile regfile_1 (
    .rs(rs), .rd(rd), .result(execute_1_p3), .clock(button_2_out), .rdval(B), .rsval(R0), .R0(R1), .R1(R2),
    .R2(R3));  // open: R3

  // Other names for the same wires on the sheet: A_t[15:0] = A_2

  // Notes on the sheet:
  //   A: default 100
  //   SD: default 1
  //   contents of Program (hex, n*v repeats v):
  //   10064,1200c8,230063,300022
  //   R
  //   =
  //   +
  //   ( R
  //   )
endmodule
